// Logisim project CPU_Library.circ as structural Verilog
module AND (
  input  [5:0] A5_A0,
  input  [5:0] B5_B0,
  output [5:0] out_3
);

  and _0 (out_3[0], A5_A0[0], B5_B0[0]);
  and _1 (out_3[1], A5_A0[1], B5_B0[1]);
  and _2 (out_3[2], A5_A0[2], B5_B0[2]);
  and _3 (out_3[3], A5_A0[3], B5_B0[3]);
  and _4 (out_3[4], A5_A0[4], B5_B0[4]);
  and _5 (out_3[5], A5_A0[5], B5_B0[5]);

  // Other names for the same wires on the sheet: A0 = A5_A0[0]; A1 = A5_A0[1]; A2 = A5_A0[2]; A3 = A5_A0[3];
  //   A4 = A5_A0[4]; A5 = A5_A0[5]; B0 = B5_B0[0]; B1 = B5_B0[1]; B2 = B5_B0[2]; B3 = B5_B0[3]; B4 = B5_B0[4];
  //   B5 = B5_B0[5]; R0 = out_3[0]; R1 = out_3[1]; R2 = out_3[2]; R3 = out_3[3]; R4 = out_3[4]; R5 = out_3[5]
endmodule
